// Logisim project 01_GATES_V.circ as structural Verilog
module main (
  input  in_1,
  input  A,
  input  in_3,
  input  B,
  input  in_5,
  input  N_Type,
  input  in_7,
  input  in_8,
  input  in_9,
  input  in_10,
  input  A_2,
  input  B_2,
  output out_13,
  output out_14,
  output out_15,
  output out_16,
  output out_17,
  output out_18,
  output out_19,
  output out_20,
  output out_21,
  output out_22,
  output out_23,
  output out_24,
  output out_25,
  output P_Type,
  output out_27,
  output out_28,
  output out_29,
  output out_30,
  output out_31,
  output out_32,
  output out_33,
  output out_34,
  output out_35,
  output out_36,
  output out_37,
  output out_38,
  output out_39,
  output out_40,
  output out_41,
  output out_42,
  output out_43,
  output out_44,
  output out_45,
  output out_46
);

  wire and_1_out, and_2_out, and_3_out, and_7_out, and_8_out, and_9_out, and_10_out, and_11_out, and_12_out,
       and_13_out, and_14_out, and_15_out, and_16_out, and_17_out, nand_3_out, nand_5_out, nor_2_out,
       nor_3_out, nor_6_out, nor_7_out, nor_8_out, nor_9_out, nor_10_out, nor_11_out, nor_12_out, not_4_out,
       not_5_out, not_6_out, not_7_out, not_8_out, not_9_out, not_10_out, not_11_out, or_1_out, or_5_out,
       or_6_out;

  Transistor #(.\type ("n")) transistor_1 (.in(1'b1), .out(out_18), .gate(N_Type));
  Pull_Resistor pull_resistor_1 (.node(out_18));
  Transistor transistor_2 (.in(1'b1), .out(P_Type), .gate(N_Type));
  Pull_Resistor pull_resistor_2 (.node(P_Type));
  xor xor_1 (out_39, A_2, B_2);
  nand nand_1 (out_33, A_2, B_2);
  nor nor_1 (out_36, A_2, B_2);
  xnor xnor_1 (out_43, A_2, B_2);
  and and_1 (and_1_out, A_2, B_2);
  or or_1 (or_1_out, A_2, B_2);
  nor nor_2 (nor_2_out, A_2, B_2);
  and and_2 (and_2_out, A_2, B_2);
  nor nor_3 (nor_3_out, A_2, B_2);
  and and_3 (and_3_out, A_2, B_2);
  not not_1 (out_13, A);
  nand nand_2 (out_16, A, B);
  nor nor_4 (out_19, A, B);
  and and_4 (out_22, A, B);
  or or_2 (out_24, A, B);
  xnor xnor_2 (out_28, A, B);
  xor xor_2 (out_30, A, B);
  not not_2 (out_34, and_1_out);
  not not_3 (out_37, or_1_out);
  nor nor_5 (out_40, nor_2_out, and_2_out);
  or or_3 (out_44, nor_3_out, and_3_out);
  NON non_1 (.in_1(A), .out_2(out_14));
  NON_ET non_et_1 (.in_1(A), .in_2(B), .out_3(out_17));
  NON_OU non_ou_1 (.in_1(A), .in_2(B), .out_3(out_20));
  ET et_1 (.in_1(A), .in_2(B), .out_3(out_23));
  OU ou_1 (.in_1(A), .in_2(B), .out_3(out_25));
  NON_OU_EX non_ou_ex_1 (.in_1(A), .in_2(B), .out_3(out_29));
  OU_EX ou_ex_1 (.in_1(A), .in_2(B), .out_3(out_31));
  not not_4 (not_4_out, A_2);
  or or_4 (out_35, not_4_out, not_5_out);
  not not_5 (not_5_out, B_2);
  not not_6 (not_6_out, A_2);
  and and_5 (out_38, not_6_out, not_7_out);
  not not_7 (not_7_out, B_2);
  or or_5 (or_5_out, A_2, B_2);
  and and_6 (out_41, or_5_out, nand_3_out);
  nand nand_3 (nand_3_out, A_2, B_2);
  or or_6 (or_6_out, A_2, B_2);
  nand nand_4 (out_45, or_6_out, nand_5_out);
  nand nand_5 (nand_5_out, A_2, B_2);
  ExactlyOne xor_3 (.out(out_15), .in0(in_1), .in1(in_3), .in2(in_5));
  and and_7 (and_7_out, in_1, nor_6_out);
  nor nor_6 (nor_6_out, in_3, in_5);
  and and_8 (and_8_out, in_3, nor_7_out);
  nor nor_7 (nor_7_out, in_1, in_5);
  and and_9 (and_9_out, in_5, nor_8_out);
  nor nor_8 (nor_8_out, in_1, in_3);
  and and_10 (and_10_out, A_2, not_8_out);
  not not_8 (not_8_out, B_2);
  not not_9 (not_9_out, A_2);
  and and_11 (and_11_out, not_9_out, B_2);
  not not_10 (not_10_out, A_2);
  and and_12 (and_12_out, not_10_out, not_11_out);
  not not_11 (not_11_out, B_2);
  and and_13 (and_13_out, A_2, B_2);
  or or_7 (out_21, and_7_out, and_8_out, and_9_out);
  or or_8 (out_42, and_10_out, and_11_out);
  or or_9 (out_46, and_12_out, and_13_out);
  nor nor_9 (nor_9_out, in_8, in_10, in_9);
  nor nor_10 (nor_10_out, in_7, in_10, in_9);
  nor nor_11 (nor_11_out, in_7, in_10, in_8);
  nor nor_12 (nor_12_out, in_8, in_7, in_9);
  ExactlyOne xor_4 (.out(out_27), .in0(in_7), .in1(in_8), .in2(in_9), .in3(in_10));
  and and_14 (and_14_out, in_7, nor_9_out);
  and and_15 (and_15_out, in_8, nor_10_out);
  and and_16 (and_16_out, in_9, nor_11_out);
  and and_17 (and_17_out, in_10, nor_12_out);
  or or_10 (out_32, and_14_out, and_15_out, and_16_out, and_17_out);
endmodule

module main2 (
  input  A,
  input  A_2,
  input  B,
  input  B_2,
  input  C,
  input  C_2,
  input  D,
  input  [3:0] A_3,
  input  [3:0] B_3,
  input  [3:0] A_4,
  input  [3:0] B_4,
  output out_12,
  output out_13,
  output out_14,
  output out_15,
  output out_16,
  output out_17,
  output out_18,
  output out_19,
  output out_20,
  output out_21,
  output out_22,
  output out_23,
  output out_24,
  output out_25,
  output out_26,
  output out_27,
  output out_28,
  output out_29,
  output out_30,
  output out_31,
  output [3:0] out_32,
  output [3:0] out_33,
  output [3:0] out_34,
  output [3:0] out_35,
  output [3:0] out_36,
  output [3:0] out_37,
  output [3:0] out_38,
  output [3:0] out_39,
  output [3:0] out_40,
  output [3:0] out_41,
  output [3:0] out_42,
  output [3:0] out_43,
  output [3:0] out_44,
  output [3:0] out_45,
  output [3:0] out_46
);

  wire and_1_out, and_2_out, and_6_out, and_8_out, and_9_out, and_10_out, or_1_out, or_2_out, or_6_out,
       or_8_out, or_9_out, or_10_out;

  and and_1 (and_1_out, A_2, B_2);
  or or_1 (or_1_out, A_2, B_2);
  and and_2 (and_2_out, A_2, B_2);
  or or_2 (or_2_out, A_2, B_2);
  and and_3 (out_12, and_1_out, C_2);
  or or_3 (out_17, or_1_out, C_2);
  nand nand_1 (out_22, and_2_out, C_2);
  nor nor_1 (out_27, or_2_out, C_2);
  assign out_32 = ~(A_3 & B_3);  // NAND_Gate nand_2, 4 bits wide
  assign out_37 = ~(A_3 | B_3);  // NOR_Gate nor_2, 4 bits wide
  assign out_41 = A_3 & B_3;  // AND_Gate and_4, 4 bits wide
  assign out_45 = A_3 | B_3;  // OR_Gate or_4, 4 bits wide
  ET_4B et_4b_1 (.in_1(A_3), .in_2(B_3), .out_3(out_42));
  OU_4B ou_4b_1 (.in_1(A_3), .in_2(B_3), .out_3(out_46));
  and and_5 (out_13, A_2, B_2, C_2);
  or or_5 (out_18, A_2, B_2, C_2);
  nand nand_3 (out_23, A_2, B_2, C_2);
  nor nor_3 (out_28, A_2, B_2, C_2);
  NON_ET_4B non_et_4b_1 (.in_1(A_3), .in_2(B_3), .out_3(out_33));
  NON_OU_4B non_ou_4b_1 (.in_1(A_3), .in_2(B_3), .out_3(out_38));
  and and_6 (and_6_out, A, B);
  and and_7 (out_14, and_6_out, and_8_out);
  and and_8 (and_8_out, C, D);
  or or_6 (or_6_out, A, B);
  or or_7 (out_19, or_6_out, or_8_out);
  or or_8 (or_8_out, C, D);
  and and_9 (and_9_out, A, B);
  nand nand_4 (out_24, and_9_out, and_10_out);
  and and_10 (and_10_out, C, D);
  or or_9 (or_9_out, A, B);
  nor nor_4 (out_29, or_9_out, or_10_out);
  or or_10 (or_10_out, C, D);
  assign out_34 = ~A_4;  // NOT_Gate not_1, 4 bits wide
  OU_EX_4B ou_ex_4b_1 (.in_1(A_4), .in_2(B_4), .out_3(out_39));
  NON_OU_EX_4B non_ou_ex_4b_1 (.in_1(A_4), .in_2(B_4), .out_3(out_43));
  NON_4B non_4b_1 (.in_1(A_4), .out_2(out_35));
  assign out_40 = A_4 ^ B_4;  // XOR_Gate xor_1, 4 bits wide
  assign out_44 = ~(A_4 ^ B_4);  // XNOR_Gate xnor_1, 4 bits wide
  and and_11 (out_15, A, B, C, D);
  or or_11 (out_20, A, B, C, D);
  nand nand_5 (out_25, A, B, C, D);
  nor nor_5 (out_30, A, B, C, D);
  ET_4 et_4_1 (.in_1(A), .in_2(B), .in_3(C), .in_4(D), .out_5(out_16));
  OU_4 ou_4_1 (.in_1(A), .in_2(B), .in_3(C), .in_4(D), .out_5(out_21));
  NON_ET_4 non_et_4_1 (.in_1(A), .in_2(B), .in_3(C), .in_4(D), .out_5(out_26));
  NON_OU_4 non_ou_4_1 (.in_1(A), .in_2(B), .in_3(C), .in_4(D), .out_5(out_31));
  assign out_36 = A_4 ^ 4'b1111;  // XOR_Gate xor_2, 4 bits wide
endmodule

module NON (
  input  in_1,
  output out_2
);

  wire transistor_2_out;

  Transistor transistor_1 (.in(1'b1), .out(out_2), .gate(in_1));
  Pull_Resistor pull_resistor_1 (.node(out_2));
  Transistor #(.\type ("n")) transistor_2 (.in(out_2), .out(transistor_2_out), .gate(in_1));
  // also tied to GND on the sheet: transistor_2_out

  // Notes on the sheet:
  //   2 Transistors
endmodule

module ET (
  input  in_1,
  input  in_2,
  output out_3
);

  wire transistor_1_out, transistor_3_out;

  Transistor #(.\type ("n"), .gate("br")) transistor_1 (.in(1'b1), .out(transistor_1_out), .gate(in_1));
  Transistor #(.\type ("n")) transistor_2 (.in(transistor_1_out), .out(out_3), .gate(in_2));
  Transistor transistor_3 (.in(out_3), .out(transistor_3_out), .gate(in_2));
  Pull_Resistor pull_resistor_1 (.node(transistor_1_out));
  Pull_Resistor pull_resistor_2 (.node(out_3));
  Transistor #(.gate("br")) transistor_4 (.in(out_3), .out(transistor_3_out), .gate(in_1));
  // also tied to GND on the sheet: transistor_3_out

  // Notes on the sheet:
  //   4 Transistors
endmodule

module NON_ET (
  input  in_1,
  input  in_2,
  output out_3
);

  wire transistor_2_out, transistor_3_out;

  Transistor transistor_1 (.in(1'b1), .out(out_3), .gate(in_1));
  Transistor #(.\type ("n")) transistor_2 (.in(out_3), .out(transistor_2_out), .gate(in_1));
  Transistor #(.\type ("n"), .gate("br")) transistor_3 (.in(transistor_2_out), .out(transistor_3_out), .gate(in_2));
  Transistor #(.gate("br")) transistor_4 (.in(1'b1), .out(out_3), .gate(in_2));
  Pull_Resistor pull_resistor_1 (.node(transistor_2_out));
  Pull_Resistor pull_resistor_2 (.node(out_3));
  // also tied to GND on the sheet: transistor_3_out

  // Notes on the sheet:
  //   4 Transistors
endmodule

module OU (
  input  in_1,
  input  in_2,
  output out_3
);

  wire transistor_2_out, transistor_3_out;

  Transistor #(.\type ("n")) transistor_1 (.in(1'b1), .out(out_3), .gate(in_1));
  Transistor transistor_2 (.in(out_3), .out(transistor_2_out), .gate(in_1));
  Transistor #(.gate("br")) transistor_3 (.in(transistor_2_out), .out(transistor_3_out), .gate(in_2));
  Transistor #(.\type ("n"), .gate("br")) transistor_4 (.in(1'b1), .out(out_3), .gate(in_2));
  Pull_Resistor pull_resistor_1 (.node(out_3));
  Pull_Resistor pull_resistor_2 (.node(transistor_2_out));
  // also tied to GND on the sheet: transistor_3_out

  // Notes on the sheet:
  //   4 Transistors
endmodule

module NON_OU (
  input  in_1,
  input  in_2,
  output out_3
);

  wire transistor_1_out, transistor_3_out;

  Transistor #(.gate("br")) transistor_1 (.in(1'b1), .out(transistor_1_out), .gate(in_1));
  Pull_Resistor pull_resistor_1 (.node(transistor_1_out));
  Transistor transistor_2 (.in(transistor_1_out), .out(out_3), .gate(in_2));
  Transistor #(.\type ("n"), .gate("br")) transistor_3 (.in(out_3), .out(transistor_3_out), .gate(in_1));
  Transistor #(.\type ("n")) transistor_4 (.in(out_3), .out(transistor_3_out), .gate(in_2));
  Pull_Resistor pull_resistor_2 (.node(out_3));
  // also tied to GND on the sheet: transistor_3_out

  // Notes on the sheet:
  //   4 Transistors
endmodule

module OU_EX (
  input  in_1,
  input  in_2,
  output out_3
);

  wire transistor_1_out, transistor_3_out, transistor_4_out, transistor_5_out, transistor_7_out;

  Transistor transistor_1 (.in(1'b1), .out(transistor_1_out), .gate(in_1));
  Transistor #(.\type ("n")) transistor_2 (.in(transistor_1_out), .out(out_3), .gate(in_2));
  Transistor #(.\type ("n")) transistor_3 (.in(out_3), .out(transistor_3_out), .gate(in_1));
  Transistor #(.\type ("n")) transistor_4 (.in(transistor_3_out), .out(transistor_4_out), .gate(in_2));
  Transistor #(.\type ("n"), .gate("br")) transistor_5 (.in(1'b1), .out(transistor_5_out), .gate(in_1));
  Pull_Resistor pull_resistor_1 (.node(transistor_1_out));
  Pull_Resistor pull_resistor_2 (.node(transistor_5_out));
  Transistor #(.gate("br")) transistor_6 (.in(transistor_5_out), .out(out_3), .gate(in_2));
  Transistor #(.gate("br")) transistor_7 (.in(out_3), .out(transistor_7_out), .gate(in_1));
  Pull_Resistor pull_resistor_3 (.node(transistor_7_out));
  Pull_Resistor pull_resistor_4 (.node(transistor_3_out));
  Transistor #(.gate("br")) transistor_8 (.in(transistor_7_out), .out(transistor_4_out), .gate(in_2));
  Pull_Resistor pull_resistor_5 (.node(out_3));
  // also tied to GND on the sheet: transistor_4_out

  // Notes on the sheet:
  //   8 Transistors
  //   OU_EX
endmodule

module NON_OU_EX (
  input  in_1,
  input  in_2,
  output out_3
);

  wire pull_resistor_1_node, pull_resistor_4_node, transistor_1_out, transistor_3_out, transistor_4_out;

  Transistor #(.\type ("n")) transistor_1 (.in(1'b1), .out(transistor_1_out), .gate(in_1));
  Pull_Resistor pull_resistor_1 (.node(pull_resistor_1_node));
  Pull_Resistor pull_resistor_2 (.node(transistor_1_out));
  Transistor #(.\type ("n")) transistor_2 (.in(transistor_1_out), .out(out_3), .gate(in_2));
  Transistor transistor_3 (.in(out_3), .out(transistor_3_out), .gate(in_1));
  Pull_Resistor pull_resistor_3 (.node(transistor_3_out));
  Pull_Resistor pull_resistor_4 (.node(pull_resistor_4_node));
  Transistor #(.\type ("n")) transistor_4 (.in(transistor_3_out), .out(transistor_4_out), .gate(in_2));
  Transistor #(.gate("br")) transistor_5 (.in(1'b1), .out(pull_resistor_1_node), .gate(in_1));
  Transistor #(.gate("br")) transistor_6 (.in(pull_resistor_1_node), .out(out_3), .gate(in_2));
  Pull_Resistor pull_resistor_5 (.node(out_3));
  Transistor #(.\type ("n"), .gate("br")) transistor_7 (.in(out_3), .out(pull_resistor_4_node), .gate(in_1));
  Transistor #(.gate("br")) transistor_8 (.in(pull_resistor_4_node), .out(transistor_4_out), .gate(in_2));
  // also tied to GND on the sheet: transistor_4_out

  // Notes on the sheet:
  //   4 Transistors
  //   NON_OU_EX
endmodule

module ET_4 (
  input  in_1,
  input  in_2,
  input  in_3,
  input  in_4,
  output out_5
);

  wire et_1_out_3, et_2_out_3;

  ET et_1 (.in_1(in_1), .in_2(in_2), .out_3(et_1_out_3));
  ET et_2 (.in_1(in_3), .in_2(in_4), .out_3(et_2_out_3));
  ET et_3 (.in_1(et_1_out_3), .in_2(et_2_out_3), .out_3(out_5));
endmodule

module NON_ET_4 (
  input  in_1,
  input  in_2,
  input  in_3,
  input  in_4,
  output out_5
);

  wire et_1_out_3, et_2_out_3;

  ET et_1 (.in_1(in_1), .in_2(in_2), .out_3(et_1_out_3));
  ET et_2 (.in_1(in_3), .in_2(in_4), .out_3(et_2_out_3));
  NON_ET non_et_1 (.in_1(et_1_out_3), .in_2(et_2_out_3), .out_3(out_5));
endmodule

module OU_4 (
  input  in_1,
  input  in_2,
  input  in_3,
  input  in_4,
  output out_5
);

  wire ou_1_out_3, ou_2_out_3;

  OU ou_1 (.in_1(in_1), .in_2(in_2), .out_3(ou_1_out_3));
  OU ou_2 (.in_1(in_3), .in_2(in_4), .out_3(ou_2_out_3));
  OU ou_3 (.in_1(ou_1_out_3), .in_2(ou_2_out_3), .out_3(out_5));
endmodule

module NON_OU_4 (
  input  in_1,
  input  in_2,
  input  in_3,
  input  in_4,
  output out_5
);

  wire ou_1_out_3, ou_2_out_3;

  OU ou_1 (.in_1(in_1), .in_2(in_2), .out_3(ou_1_out_3));
  OU ou_2 (.in_1(in_3), .in_2(in_4), .out_3(ou_2_out_3));
  NON_OU non_ou_1 (.in_1(ou_1_out_3), .in_2(ou_2_out_3), .out_3(out_5));
endmodule

module NON_4B (
  input  [3:0] in_1,
  output [3:0] out_2
);

  NON non_1 (.in_1(in_1[0]), .out_2(out_2[0]));
  NON non_2 (.in_1(in_1[1]), .out_2(out_2[1]));
  NON non_3 (.in_1(in_1[2]), .out_2(out_2[2]));
  NON non_4 (.in_1(in_1[3]), .out_2(out_2[3]));
endmodule

module ET_4B (
  input  [3:0] in_1,
  input  [3:0] in_2,
  output [3:0] out_3
);

  ET et_1 (.in_1(in_1[0]), .in_2(in_2[0]), .out_3(out_3[0]));
  ET et_2 (.in_1(in_1[1]), .in_2(in_2[1]), .out_3(out_3[1]));
  ET et_3 (.in_1(in_1[2]), .in_2(in_2[2]), .out_3(out_3[2]));
  ET et_4 (.in_1(in_1[3]), .in_2(in_2[3]), .out_3(out_3[3]));
endmodule

module NON_ET_4B (
  input  [3:0] in_1,
  input  [3:0] in_2,
  output [3:0] out_3
);

  NON_ET non_et_1 (.in_1(in_1[0]), .in_2(in_2[0]), .out_3(out_3[0]));
  NON_ET non_et_2 (.in_1(in_1[1]), .in_2(in_2[1]), .out_3(out_3[1]));
  NON_ET non_et_3 (.in_1(in_1[2]), .in_2(in_2[2]), .out_3(out_3[2]));
  NON_ET non_et_4 (.in_1(in_1[3]), .in_2(in_2[3]), .out_3(out_3[3]));
endmodule

module OU_4B (
  input  [3:0] in_1,
  input  [3:0] in_2,
  output [3:0] out_3
);

  OU ou_1 (.in_1(in_1[0]), .in_2(in_2[0]), .out_3(out_3[0]));
  OU ou_2 (.in_1(in_1[1]), .in_2(in_2[1]), .out_3(out_3[1]));
  OU ou_3 (.in_1(in_1[2]), .in_2(in_2[2]), .out_3(out_3[2]));
  OU ou_4 (.in_1(in_1[3]), .in_2(in_2[3]), .out_3(out_3[3]));
endmodule

module NON_OU_4B (
  input  [3:0] in_1,
  input  [3:0] in_2,
  output [3:0] out_3
);

  NON_OU non_ou_1 (.in_1(in_1[0]), .in_2(in_2[0]), .out_3(out_3[0]));
  NON_OU non_ou_2 (.in_1(in_1[1]), .in_2(in_2[1]), .out_3(out_3[1]));
  NON_OU non_ou_3 (.in_1(in_1[2]), .in_2(in_2[2]), .out_3(out_3[2]));
  NON_OU non_ou_4 (.in_1(in_1[3]), .in_2(in_2[3]), .out_3(out_3[3]));
endmodule

module OU_EX_4B (
  input  [3:0] in_1,
  input  [3:0] in_2,
  output [3:0] out_3
);

  OU_EX ou_ex_1 (.in_1(in_1[0]), .in_2(in_2[0]), .out_3(out_3[0]));
  OU_EX ou_ex_2 (.in_1(in_1[1]), .in_2(in_2[1]), .out_3(out_3[1]));
  OU_EX ou_ex_3 (.in_1(in_1[2]), .in_2(in_2[2]), .out_3(out_3[2]));
  OU_EX ou_ex_4 (.in_1(in_1[3]), .in_2(in_2[3]), .out_3(out_3[3]));
endmodule

module NON_OU_EX_4B (
  input  [3:0] in_1,
  input  [3:0] in_2,
  output [3:0] out_3
);

  NON_OU_EX non_ou_ex_1 (.in_1(in_1[0]), .in_2(in_2[0]), .out_3(out_3[0]));
  NON_OU_EX non_ou_ex_2 (.in_1(in_1[1]), .in_2(in_2[1]), .out_3(out_3[1]));
  NON_OU_EX non_ou_ex_3 (.in_1(in_1[2]), .in_2(in_2[2]), .out_3(out_3[2]));
  NON_OU_EX non_ou_ex_4 (.in_1(in_1[3]), .in_2(in_2[3]), .out_3(out_3[3]));
endmodule
