// Logisim project 04_ARITHMETIC_00_V.circ as structural Verilog: 33 circuits, main circuit main
module main (
  input  [3:0] in_1,
  input  [3:0] in_2,
  input  [3:0] in_3,
  input  [3:0] in_4,
  input  [3:0] in_5,
  input  in_6,
  input  [7:0] in_7,
  input  [7:0] in_8,
  input  in_9,
  input  [7:0] in_10,
  input  [7:0] in_11,
  output out_12,
  output out_13,
  output out_14,
  output out_15,
  output out_16,
  output [7:0] out_17,
  output [7:0] out_18
);

  wire add4b_2_carry_out, sub4b2_1_carry_out;
  wire [3:0] add4b2_1_output, add4b_1_output, addb_1_output, adder_1_out, neg4_1_output, negator_1_out,
       sub4a_1_output, sub4sa_1_output, subtractor_1_out;

  // Probe on in_1
  // Probe on in_1
  // Probe on in_1
  // Probe on in_2
  // Probe on in_2
  // Probe on in_2
  // Probe on in_3
  // Probe on in_3
  // Probe on in_3
  // Probe on in_4
  // Probe on in_4
  // Probe on in_4
  Adder #(.width(4)) adder_1 (.a(in_1), .b(in_2), .out(adder_1_out), .cin(1'b0), .cout(out_12));
  ADDB addb_1 (.Output(addb_1_output), .Input_A(in_1), .Input_B(in_2));
  Subtractor #(.width(4)) subtractor_1 (.a(in_3), .b(in_4), .out(subtractor_1_out), .bin(1'b0), .bout(out_15));
  // Probe on subtractor_1_out
  // Probe on subtractor_1_out
  // Probe on subtractor_1_out
  // Probe on subtractor_1_out
  // Probe on in_7
  // Probe on in_8
  // Probe on in_10
  // Probe on in_11
  // Probe on adder_1_out
  // Probe on adder_1_out
  // Probe on adder_1_out
  // Probe on adder_1_out
  // Probe on addb_1_output
  // Probe on addb_1_output
  // Probe on addb_1_output
  // Probe on addb_1_output
  SUB4A sub4a_1 (.Borrow_In(1'b0), .Minuend(in_3), .Subtrahend(in_4), .Output(sub4a_1_output), .Borrow_Out(out_16));
  ADD4B add4b_1 (.Carry_In(1'b0), .Input_A(in_1), .Input_B(in_2), .Output(add4b_1_output), .Carry_Out(out_13));
  // Probe on sub4a_1_output
  // Probe on sub4a_1_output
  // Probe on sub4a_1_output
  // Probe on sub4a_1_output
  ADD4B add4b_2 (
    .Carry_In(in_6), .Input_A(in_7[3:0]), .Input_B(in_8[3:0]), .Output(out_17[3:0]),
    .Carry_Out(add4b_2_carry_out));
  ADD4B add4b_3 (
    .Carry_In(add4b_2_carry_out), .Input_A(in_7[7:4]), .Input_B(in_8[7:4]), .Output(out_17[7:4]));  // open: Carry_Out
  SUB4B2 sub4b2_1 (
    .Carry_In(in_9), .Input_A(in_10[3:0]), .Input_B(in_11[3:0]), .Output(out_18[3:0]),
    .Carry_Out(sub4b2_1_carry_out));
  SUB4B2 sub4b2_2 (
    .Carry_In(sub4b2_1_carry_out), .Input_A(in_10[7:4]), .Input_B(in_11[7:4]), .Output(out_18[7:4]));  // open: Carry_Out
  // Probe on add4b_1_output
  // Probe on add4b_1_output
  // Probe on add4b_1_output
  // Probe on add4b_1_output
  SUB4SA sub4sa_1 (.Minuend(in_3), .Subtrahend(in_4), .Output(sub4sa_1_output));
  // Probe on out_17
  ADD4B2 add4b2_1 (.Carry_In(1'b0), .Input_A(in_1), .Output(add4b2_1_output), .Input_B(in_2), .Carry_Out(out_14));
  // Probe on add4b2_1_output
  // Probe on add4b2_1_output
  // Probe on add4b2_1_output
  // Probe on add4b2_1_output
  // Probe on sub4sa_1_output
  // Probe on sub4sa_1_output
  // Probe on sub4sa_1_output
  // Probe on sub4sa_1_output
  // Probe on out_18
  // Probe on in_5
  // Probe on in_5
  // Probe on in_5
  Negator #(.width(4)) negator_1 (.in(in_5), .out(negator_1_out));
  // Probe on negator_1_out
  // Probe on negator_1_out
  // Probe on negator_1_out
  // Probe on negator_1_out
  NEG4 neg4_1 (.Input(in_5), .Output(neg4_1_output));
  // Probe on neg4_1_output
  // Probe on neg4_1_output
  // Probe on neg4_1_output
  // Probe on neg4_1_output
endmodule

module main2 (
);

  wire C0, C1, C2, C3, C4, C5, C6, C7, C8;
  wire [7:0] L1_0, L1_1, L1_2, L1_3, L1_4, L1_5, L1_6, L1_7, L1_8, L2_0, L2_1, L2_2, L2_3, L2_4, L2_5, L2_6,
       L2_7, L2_8, negator_1_out, R0, R1, R2, R3, R4, R5, R6, R7, R8;

  // Probe on L1_0
  // Probe on L1_0
  // Probe on L2_0
  // Probe on L2_0
  // Probe on L1_1
  // Probe on L1_1
  // Probe on L2_1
  // Probe on L2_1
  // Probe on L1_2
  // Probe on L1_2
  // Probe on L2_2
  // Probe on L2_2
  // Probe on C0
  Adder adder_1 (.a(L1_0), .b(L2_0), .out(R0), .cin(1'b0), .cout(C0));
  // Probe on C1
  Adder adder_2 (.a(L1_1), .b(L2_1), .out(R1), .cin(1'b0), .cout(C1));
  // Probe on C2
  Adder adder_3 (.a(L1_2), .b(L2_2), .out(R2), .cin(1'b0), .cout(C2));
  // Probe on R0
  // Probe on R0
  // Probe on R0
  // Probe on R1
  // Probe on R1
  // Probe on R1
  // Probe on R2
  // Probe on R2
  // Probe on R2
  // Probe on L1_6
  // Probe on L1_6
  // Probe on L2_6
  // Probe on L2_6
  // Probe on L1_7
  // Probe on L1_7
  // Probe on L2_7
  // Probe on L2_7
  // Probe on L1_8
  // Probe on L1_8
  // Probe on L2_8
  // Probe on L2_8
  // Probe on C6
  Adder adder_4 (.a(L1_6), .b(L2_6), .out(R6), .cin(1'b0), .cout(C6));
  // Probe on C7
  Adder adder_5 (.a(L1_7), .b(L2_7), .out(R7), .cin(1'b0), .cout(C7));
  // Probe on C8
  Adder adder_6 (.a(L1_8), .b(L2_8), .out(R8), .cin(1'b0), .cout(C8));
  // Probe on L1_3
  // Probe on L1_3
  // Probe on L2_3
  // Probe on L2_3
  // Probe on L1_4
  // Probe on L1_4
  // Probe on L2_4
  // Probe on L2_4
  // Probe on L1_5
  // Probe on L1_5
  // Probe on L2_5
  // Probe on L2_5
  Adder adder_7 (.a(L1_3), .b(L2_3), .out(R3), .cin(1'b0), .cout(C3));
  Adder adder_8 (.a(L1_4), .b(L2_4), .out(R4), .cin(1'b0), .cout(C4));
  Adder adder_9 (.a(L1_5), .b(L2_5), .out(R5), .cin(1'b0), .cout(C5));
  // Probe on R6
  // Probe on R6
  // Probe on R6
  // Probe on R7
  // Probe on R7
  // Probe on R7
  // Probe on R8
  // Probe on R8
  // Probe on R8
  // Probe on C3
  // Probe on C4
  // Probe on C5
  Negator negator_1 (.in(R7), .out(negator_1_out));
  // Probe on R3
  // Probe on R3
  // Probe on R3
  // Probe on R4
  // Probe on R4
  // Probe on R4
  // Probe on R5
  // Probe on R5
  // Probe on R5
  // Probe on negator_1_out
  // Probe on negator_1_out
  // Probe on negator_1_out
  // Probe on L1_0
  // Probe on L2_0
  // Probe on R0
  // Probe on C0
  // Probe on L1_1
  // Probe on L2_1
  // Probe on R1
  // Probe on C1
  // Probe on L1_2
  // Probe on L2_2
  // Probe on R2
  // Probe on C2
  // Probe on L1_3
  // Probe on L2_3
  // Probe on R3
  // Probe on C3
  // Probe on L1_4
  // Probe on L2_4
  // Probe on R4
  // Probe on C4
  // Probe on L1_0
  // Probe on L2_0
  // Probe on R0
  // Probe on L1_1
  // Probe on L2_1
  // Probe on R1
  // Probe on L1_2
  // Probe on L2_2
  // Probe on R2
  // Probe on L1_3
  // Probe on L2_3
  // Probe on R3
  // Probe on L1_4
  // Probe on L2_4
  // Probe on R4
  // Probe on L1_5
  // Probe on L2_5
  // Probe on R5
  // Probe on C5
  // Probe on L1_6
  // Probe on L2_6
  // Probe on R6
  // Probe on C6
  // Probe on L1_7
  // Probe on L2_7
  // Probe on R7
  // Probe on C7
  // Probe on L1_8
  // Probe on L2_8
  // Probe on R8
  // Probe on C8
  // Probe on L1_5
  // Probe on L2_5
  // Probe on R5
  // Probe on L1_6
  // Probe on L2_6
  // Probe on R6
  // Probe on L1_7
  // Probe on L2_7
  // Probe on R7
  // Probe on L1_8
  // Probe on L2_8
  // Probe on R8
  list1 list1_1 (
    .out_1(L1_0), .out_2(L1_1), .out_3(L1_2), .out_4(L1_3), .out_5(L1_4), .out_6(L1_5), .out_7(L1_6),
    .out_8(L1_7), .out_9(L1_8));
  list2 list2_1 (
    .out_1(L2_0), .out_2(L2_1), .out_3(L2_2), .out_4(L2_3), .out_5(L2_4), .out_6(L2_5), .out_7(L2_6),
    .out_8(L2_7), .out_9(L2_8));
endmodule

module ADDB (
  input  [3:0] Input_A,
  input  [3:0] Input_B,
  output [3:0] Output
);

  wire and_1_out, and_2_out, and_3_out, and_4_out, and_6_out, and_7_out, and_8_out, and_9_out, and_10_out,
       and_11_out, not_1_out, not_2_out, not_3_out, not_4_out, not_5_out, not_6_out, not_7_out, or_1_out,
       or_2_out, or_3_out, or_4_out, or_5_out, or_6_out, or_7_out, or_8_out, or_9_out;

  or or_1 (or_1_out, Input_A[0], Input_B[0]);
  and and_1 (and_1_out, Input_A[0], Input_B[0]);
  or or_2 (or_2_out, Input_A[1], Input_B[1]);
  and and_2 (and_2_out, Input_A[1], Input_B[1]);
  or or_3 (or_3_out, Input_A[2], Input_B[2]);
  and and_3 (and_3_out, Input_A[2], Input_B[2]);
  or or_4 (or_4_out, Input_A[3], Input_B[3]);
  and and_4 (and_4_out, Input_A[3], Input_B[3]);
  not not_1 (not_1_out, and_1_out);
  not not_2 (not_2_out, and_2_out);
  or or_5 (or_5_out, and_7_out, and_2_out);
  not not_3 (not_3_out, and_3_out);
  or or_6 (or_6_out, and_8_out, and_3_out);
  not not_4 (not_4_out, and_4_out);
  and and_5 (Output[0], or_1_out, not_1_out);
  or or_7 (or_7_out, and_1_out, and_6_out);
  and and_6 (and_6_out, or_2_out, not_2_out);
  and and_7 (and_7_out, and_1_out, and_6_out);
  or or_8 (or_8_out, or_5_out, and_9_out);
  and and_8 (and_8_out, or_5_out, and_9_out);
  and and_9 (and_9_out, or_3_out, not_3_out);
  or or_9 (or_9_out, or_6_out, and_10_out);
  and and_10 (and_10_out, or_4_out, not_4_out);
  and and_11 (and_11_out, or_6_out, and_10_out);
  and and_12 (Output[1], or_7_out, not_5_out);
  not not_5 (not_5_out, and_7_out);
  and and_13 (Output[2], or_8_out, not_6_out);
  not not_6 (not_6_out, and_8_out);
  and and_14 (Output[3], or_9_out, not_7_out);
  not not_7 (not_7_out, and_11_out);
endmodule

module ADD0 (
  input  Carry_In,
  input  Input_A,
  input  Input_B,
  output Output,
  output Carry_Out
);

  wire and_1_out, and_2_out, nor_1_out, nor_2_out, nor_3_out;

  and and_1 (and_1_out, Input_A, Input_B);
  nor nor_1 (nor_1_out, Input_A, Input_B);
  nor nor_2 (nor_2_out, nor_1_out, and_1_out);
  nor nor_3 (nor_3_out, Carry_In, nor_2_out);
  and and_2 (and_2_out, Carry_In, nor_2_out);
  nor nor_4 (Output, nor_3_out, and_2_out);
  or or_1 (Carry_Out, and_2_out, and_1_out);

  // Notes on the sheet:
  //   0+0=0 (R=0)
  //   0+1=1 (R=0)
  //   1+0=1 (R=0)
  //   1+1=0 (R=1)
  //   28 Transistors
  //   ADD : 2 * 4 Transistors = 8 Transistors
  //   OR : 1 * 4 Transistors = 4 Transistors
  //   NOR : 4 * 4 Transistors = 16 Transistors
  //   Total : 4 + 8 + 16 = 28 Transistors
endmodule

module ADD1 (
  input  Carry_In,
  input  Input_A,
  input  Input_B,
  output Output,
  output Carry_Out
);

  wire and_1_out, and_2_out, xor_1_out;

  xor xor_1 (xor_1_out, Input_A, Input_B);
  and and_1 (and_1_out, Input_A, Input_B);
  xor xor_2 (Output, Carry_In, xor_1_out);
  and and_2 (and_2_out, Carry_In, xor_1_out);
  or or_1 (Carry_Out, and_2_out, and_1_out);

  // Notes on the sheet:
  //   0+0=0 (R=0)
  //   0+1=1 (R=0)
  //   1+0=1 (R=0)
  //   1+1=0 (R=1)
  //   28 Transistors
  //   ADD : 2 * 4 Transistors = 8 Transistors
  //   OR : 1 * 4 Transistors = 4 Transistors
  //   XOR : 2 * 8 Transistors = 16 Transistors
  //   Total : 4 + 8 + 16 = 28 Transistors
endmodule

module ADD2 (
  input  Carry_In,
  input  Input_A,
  input  Input_B,
  output Output,
  output Carry_Out
);

  wire and_1_out, and_2_out, and_3_out, not_1_out, not_2_out, or_1_out, or_2_out;

  or or_1 (or_1_out, Input_A, Input_B);
  and and_1 (and_1_out, Input_A, Input_B);
  and and_2 (and_2_out, or_1_out, not_1_out);
  not not_1 (not_1_out, and_1_out);
  or or_2 (or_2_out, Carry_In, and_2_out);
  and and_3 (and_3_out, Carry_In, and_2_out);
  not not_2 (not_2_out, and_3_out);
  and and_4 (Output, or_2_out, not_2_out);
  or or_3 (Carry_Out, and_3_out, and_1_out);

  // Notes on the sheet:
  //   0+0=0 (R=0)
  //   0+1=1 (R=0)
  //   1+0=1 (R=0)
  //   1+1=0 (R=1)
  //   32 Transistors
  //   ADD : 4 * 4 Transistors = 16 Transistors
  //   OR : 3 * 4 Transistors = 12 Transistors
  //   NOT : 2 * 2 Transistors = 4 Transistors
  //   Total : 4 + 12 + 16 = 32 Transistors
endmodule

module ADDSP0 (
  input  Input_A,
  input  Input_B,
  output Output,
  output Carry_Out
);

  wire nor_1_out;

  nor nor_1 (nor_1_out, Input_A, Input_B);
  and and_1 (Carry_Out, Input_A, Input_B);
  nor nor_2 (Output, nor_1_out, Carry_Out);

  // Notes on the sheet:
  //   0+0=0 (R=0)
  //   0+1=1 (R=0)
  //   1+0=1 (R=0)
  //   1+1=0 (R=1)
endmodule

module ADDSP1 (
  input  Input_A,
  input  Input_B,
  output Output,
  output Carry_Out
);

  xor xor_1 (Output, Input_A, Input_B);
  and and_1 (Carry_Out, Input_A, Input_B);
endmodule

module ADDSP2 (
  input  Input_A,
  input  Input_B,
  output Output,
  output Carry_Out
);

  wire not_1_out, or_1_out;

  or or_1 (or_1_out, Input_A, Input_B);
  and and_1 (Carry_Out, Input_A, Input_B);
  and and_2 (Output, or_1_out, not_1_out);
  not not_1 (not_1_out, Carry_Out);

  // Notes on the sheet:
  //   0+0=0 (R=0)
  //   0+1=1 (R=0)
  //   1+0=1 (R=0)
  //   1+1=0 (R=1)
endmodule

module ADDSR0 (
  input  Carry_In,
  input  Input_A,
  input  Input_B,
  output Output
);

  wire and_1_out, and_2_out, nor_1_out, nor_2_out, nor_3_out;

  and and_1 (and_1_out, Input_A, Input_B);
  nor nor_1 (nor_1_out, Input_A, Input_B);
  nor nor_2 (nor_2_out, nor_1_out, and_1_out);
  nor nor_3 (nor_3_out, Carry_In, nor_2_out);
  and and_2 (and_2_out, Carry_In, nor_2_out);
  nor nor_4 (Output, nor_3_out, and_2_out);
endmodule

module ADDSR1 (
  input  Carry_In,
  input  Input_A,
  input  Input_B,
  output Output
);

  wire xor_1_out;

  xor xor_1 (xor_1_out, Input_A, Input_B);
  xor xor_2 (Output, Carry_In, xor_1_out);
endmodule

module ADDSR2 (
  input  Carry_In,
  input  Input_A,
  input  Input_B,
  output Output
);

  wire and_1_out, and_2_out, and_3_out, not_1_out, not_2_out, or_1_out, or_2_out;

  or or_1 (or_1_out, Input_A, Input_B);
  and and_1 (and_1_out, Input_A, Input_B);
  and and_2 (and_2_out, or_1_out, not_1_out);
  not not_1 (not_1_out, and_1_out);
  or or_2 (or_2_out, Carry_In, and_2_out);
  not not_2 (not_2_out, and_3_out);
  and and_3 (and_3_out, Carry_In, and_2_out);
  and and_4 (Output, or_2_out, not_2_out);
endmodule

module ADDTR (
  input  Carry_In,
  input  Input_A,
  input  Input_B,
  output Output,
  output Carry_Out
);

  wire pull_resistor_12_node, transistor_1_out, transistor_2_out, transistor_3_out, transistor_5_out,
       transistor_6_out, transistor_7_out, transistor_9_out, transistor_10_out, transistor_11_out,
       transistor_13_out, transistor_14_out, transistor_15_out, transistor_17_out, transistor_18_out,
       transistor_19_out, transistor_21_out, transistor_23_out, transistor_28_out;

  Transistor #(.gate("br")) transistor_1 (.in(1'b1), .out(transistor_1_out), .gate(Input_A));
  Pull_Resistor pull_resistor_1 (.node(transistor_1_out));
  Transistor transistor_2 (.in(transistor_1_out), .out(transistor_2_out), .gate(Input_B));
  Transistor #(.\type ("n")) transistor_3 (.in(transistor_2_out), .out(transistor_3_out), .gate(Input_B));
  Transistor #(.\type ("n"), .gate("br")) transistor_4 (.in(transistor_2_out), .out(transistor_3_out), .gate(Input_A));
  Transistor #(.\type ("n"), .gate("br")) transistor_5 (.in(1'b1), .out(transistor_5_out), .gate(Input_A));
  Pull_Resistor pull_resistor_2 (.node(transistor_5_out));
  Transistor #(.\type ("n")) transistor_6 (.in(transistor_5_out), .out(transistor_6_out), .gate(Input_B));
  Transistor transistor_7 (.in(transistor_6_out), .out(transistor_7_out), .gate(Input_B));
  Pull_Resistor pull_resistor_3 (.node(transistor_2_out));
  Pull_Resistor pull_resistor_4 (.node(transistor_6_out));
  Transistor #(.gate("br")) transistor_8 (.in(transistor_6_out), .out(transistor_7_out), .gate(Input_A));
  Transistor #(.gate("br")) transistor_9 (.in(1'b1), .out(transistor_9_out), .gate(transistor_2_out));
  Pull_Resistor pull_resistor_5 (.node(transistor_9_out));
  Transistor transistor_10 (.in(transistor_9_out), .out(transistor_10_out), .gate(transistor_6_out));
  Transistor #(.\type ("n")) transistor_11 (.in(transistor_10_out), .out(transistor_11_out), .gate(transistor_6_out));
  Pull_Resistor pull_resistor_6 (.node(transistor_10_out));
  Transistor #(.\type ("n"), .gate("br")) transistor_12 (
    .in(transistor_10_out), .out(transistor_11_out), .gate(transistor_2_out));
  Transistor #(.gate("br")) transistor_13 (.in(1'b1), .out(transistor_13_out), .gate(Carry_In));
  Transistor transistor_14 (.in(transistor_13_out), .out(transistor_14_out), .gate(transistor_10_out));
  Transistor #(.\type ("n")) transistor_15 (.in(transistor_14_out), .out(transistor_15_out), .gate(transistor_10_out));
  Pull_Resistor pull_resistor_7 (.node(transistor_13_out));
  Pull_Resistor pull_resistor_8 (.node(transistor_14_out));
  Transistor #(.\type ("n"), .gate("br")) transistor_16 (
    .in(transistor_14_out), .out(transistor_15_out), .gate(Carry_In));
  Transistor #(.\type ("n"), .gate("br")) transistor_17 (.in(1'b1), .out(transistor_17_out), .gate(Carry_In));
  Pull_Resistor pull_resistor_9 (.node(transistor_17_out));
  Transistor #(.\type ("n")) transistor_18 (.in(transistor_17_out), .out(transistor_18_out), .gate(transistor_10_out));
  Transistor transistor_19 (.in(transistor_18_out), .out(transistor_19_out), .gate(transistor_10_out));
  Transistor #(.gate("br")) transistor_20 (.in(transistor_18_out), .out(transistor_19_out), .gate(Carry_In));
  Pull_Resistor pull_resistor_10 (.node(transistor_18_out));
  Transistor #(.gate("br")) transistor_21 (.in(1'b1), .out(transistor_21_out), .gate(transistor_14_out));
  Pull_Resistor pull_resistor_11 (.node(transistor_21_out));
  Transistor transistor_22 (.in(transistor_21_out), .out(Output), .gate(transistor_18_out));
  Transistor #(.\type ("n")) transistor_23 (.in(Output), .out(transistor_23_out), .gate(transistor_18_out));
  Transistor #(.\type ("n"), .gate("br")) transistor_24 (
    .in(Output), .out(transistor_23_out), .gate(transistor_14_out));
  Transistor #(.\type ("n"), .gate("br")) transistor_25 (.in(1'b1), .out(Carry_Out), .gate(transistor_6_out));
  Transistor #(.\type ("n")) transistor_26 (.in(1'b1), .out(Carry_Out), .gate(transistor_18_out));
  Pull_Resistor pull_resistor_12 (.node(pull_resistor_12_node));
  Transistor transistor_27 (.in(Carry_Out), .out(pull_resistor_12_node), .gate(transistor_18_out));
  Transistor #(.gate("br")) transistor_28 (
    .in(pull_resistor_12_node), .out(transistor_28_out), .gate(transistor_6_out));
  Pull_Resistor pull_resistor_13 (.node(Output));
  Pull_Resistor pull_resistor_14 (.node(Carry_Out));
  // also tied to GND on the sheet: {transistor_3_out, transistor_7_out, transistor_11_out, transistor_15_out, transistor_19_out, transistor_23_out, transistor_28_out}

  // Notes on the sheet:
  //   4 Transistors
  //   4 Transistors
  //   4 Transistors
  //   4 Transistors
  //   4 Transistors
  //   4 Transistors
  //   4 Transistors
endmodule

module ADD2B (
  input  Carry_In,
  input  [1:0] Input_A,
  input  [1:0] Input_B,
  output [1:0] Output,
  output Carry_Out
);

  wire add0_1_carry_out;

  ADD0 add0_1 (
    .Carry_In(Carry_In), .Input_A(Input_A[0]), .Input_B(Input_B[0]), .Output(Output[0]),
    .Carry_Out(add0_1_carry_out));
  ADD0 add0_2 (
    .Carry_In(add0_1_carry_out), .Input_A(Input_A[1]), .Input_B(Input_B[1]), .Output(Output[1]),
    .Carry_Out(Carry_Out));
endmodule

module ADD4B (
  input  Carry_In,
  input  [3:0] Input_A,
  input  [3:0] Input_B,
  output [3:0] Output,
  output Carry_Out
);

  wire add0_1_carry_out, add0_2_carry_out, add0_3_carry_out;

  ADD0 add0_1 (
    .Carry_In(Carry_In), .Input_A(Input_A[0]), .Input_B(Input_B[0]), .Output(Output[0]),
    .Carry_Out(add0_1_carry_out));
  ADD0 add0_2 (
    .Carry_In(add0_1_carry_out), .Input_A(Input_A[1]), .Input_B(Input_B[1]), .Output(Output[1]),
    .Carry_Out(add0_2_carry_out));
  ADD0 add0_3 (
    .Carry_In(add0_2_carry_out), .Input_A(Input_A[2]), .Input_B(Input_B[2]), .Output(Output[2]),
    .Carry_Out(add0_3_carry_out));
  ADD0 add0_4 (
    .Carry_In(add0_3_carry_out), .Input_A(Input_A[3]), .Input_B(Input_B[3]), .Output(Output[3]),
    .Carry_Out(Carry_Out));
endmodule

module ADD4B2 (
  input  Carry_In,
  input  [3:0] Input_A,
  input  [3:0] Input_B,
  output [3:0] Output,
  output Carry_Out
);

  wire add2b_1_carry_out;

  ADD2B add2b_1 (
    .Carry_In(Carry_In), .Input_A(Input_A[1:0]), .Input_B(Input_B[1:0]), .Output(Output[1:0]),
    .Carry_Out(add2b_1_carry_out));
  ADD2B add2b_2 (
    .Carry_In(add2b_1_carry_out), .Input_A(Input_A[3:2]), .Input_B(Input_B[3:2]), .Output(Output[3:2]),
    .Carry_Out(Carry_Out));
endmodule

module CEPS4B (
  input  Input_A0,
  input  Input_A0_2,
  input  Input_B0,
  input  Input_B0_2,
  input  Input_A1,
  input  Input_A1_2,
  input  Input_B1,
  input  Input_B1_2,
  input  Input_A2,
  input  Input_A2_2,
  input  Input_B2,
  input  Input_B2_2,
  input  Input_A3,
  input  Input_A3_2,
  input  Input_B3,
  input  Input_B3_2,
  input  Input_A4,
  input  Input_A4_2,
  input  Input_B4,
  input  Input_B4_2,
  output Output0,
  output Output0_2,
  output Output1,
  output Output1_2,
  output Output2,
  output Output2_2,
  output Output3,
  output Output3_2,
  output Output4,
  output Output4_2
);

  wire add2_1_carry_out, add2_2_carry_out, add2_3_carry_out, addsp2_1_carry_out, and_1_out, and_2_out,
       and_3_out, and_4_out, and_5_out, and_7_out, and_8_out, and_9_out, and_10_out, and_11_out, and_12_out,
       and_13_out, and_14_out, not_1_out, not_2_out, not_3_out, not_4_out, not_5_out, not_6_out, not_7_out,
       not_8_out, not_9_out, or_1_out, or_2_out, or_3_out, or_4_out, or_5_out, or_6_out, or_7_out, or_8_out,
       or_9_out, or_10_out, or_11_out, or_12_out;

  or or_1 (or_1_out, Input_A0, Input_B0_2);
  and and_1 (and_1_out, Input_A0, Input_B0_2);
  or or_2 (or_2_out, Input_A1_2, Input_B1_2);
  and and_2 (and_2_out, Input_A1_2, Input_B1_2);
  or or_3 (or_3_out, Input_A2_2, Input_B2_2);
  and and_3 (and_3_out, Input_A2_2, Input_B2_2);
  or or_4 (or_4_out, Input_A3_2, Input_B3_2);
  and and_4 (and_4_out, Input_A3_2, Input_B3_2);
  or or_5 (or_5_out, Input_A4_2, Input_B4_2);
  not not_1 (not_1_out, and_5_out);
  and and_5 (and_5_out, Input_A4_2, Input_B4_2);
  and and_6 (Output0, or_1_out, not_2_out);
  not not_2 (not_2_out, and_1_out);
  and and_7 (and_7_out, or_2_out, not_3_out);
  not not_3 (not_3_out, and_2_out);
  and and_8 (and_8_out, or_3_out, not_4_out);
  not not_4 (not_4_out, and_3_out);
  and and_9 (and_9_out, or_4_out, not_5_out);
  not not_5 (not_5_out, and_4_out);
  and and_10 (and_10_out, or_5_out, not_1_out);
  or or_6 (or_6_out, and_1_out, and_7_out);
  and and_11 (and_11_out, and_1_out, and_7_out);
  not not_6 (not_6_out, and_11_out);
  or or_7 (or_7_out, or_10_out, and_8_out);
  not not_7 (not_7_out, and_12_out);
  and and_12 (and_12_out, or_10_out, and_8_out);
  or or_8 (or_8_out, or_11_out, and_9_out);
  not not_8 (not_8_out, and_13_out);
  and and_13 (and_13_out, or_11_out, and_9_out);
  or or_9 (or_9_out, or_12_out, and_10_out);
  not not_9 (not_9_out, and_14_out);
  and and_14 (and_14_out, or_12_out, and_10_out);
  and and_15 (Output1, or_6_out, not_6_out);
  or or_10 (or_10_out, and_11_out, and_2_out);
  and and_16 (Output2, or_7_out, not_7_out);
  or or_11 (or_11_out, and_12_out, and_3_out);
  and and_17 (Output3, or_8_out, not_8_out);
  or or_12 (or_12_out, and_13_out, and_4_out);
  and and_18 (Output4, or_9_out, not_9_out);
  ADDSP2 addsp2_1 (.Input_A(Input_A0_2), .Input_B(Input_B0), .Output(Output0_2), .Carry_Out(addsp2_1_carry_out));
  ADD2 add2_1 (
    .Carry_In(addsp2_1_carry_out), .Input_A(Input_A1), .Input_B(Input_B1), .Output(Output1_2),
    .Carry_Out(add2_1_carry_out));
  ADD2 add2_2 (
    .Carry_In(add2_1_carry_out), .Input_A(Input_A2), .Input_B(Input_B2), .Output(Output2_2),
    .Carry_Out(add2_2_carry_out));
  ADD2 add2_3 (
    .Carry_In(add2_2_carry_out), .Input_A(Input_A3), .Input_B(Input_B3), .Output(Output3_2),
    .Carry_Out(add2_3_carry_out));
  ADDSR2 addsr2_1 (.Carry_In(add2_3_carry_out), .Input_A(Input_A4), .Input_B(Input_B4), .Output(Output4_2));
endmodule

module NEG4 (
  input  [3:0] Input,
  output [3:0] Output
);

  wire [3:0] not_1_out;

  assign not_1_out = ~Input;  // NOT_Gate not_1, 4 bits wide
  Adder #(.width(4)) adder_1 (.a(not_1_out), .b(4'b0001), .out(Output), .cin(1'b0));  // open: cout
endmodule

module NEG42 (
  input  [3:0] Input,
  output [3:0] Output
);

  wire [3:0] xor_1_out;

  assign xor_1_out = 4'b1111 ^ Input;  // XOR_Gate xor_1, 4 bits wide
  Adder #(.width(4)) adder_1 (.a(xor_1_out), .b(4'b0001), .out(Output), .cin(1'b0));  // open: cout
endmodule

module SUB4SA (
  input  [3:0] Minuend,
  input  [3:0] Subtrahend,
  output [3:0] Output
);

  wire [3:0] negator_1_out;

  Negator #(.width(4)) negator_1 (.in(Subtrahend), .out(negator_1_out));
  Adder #(.width(4)) adder_1 (.a(Minuend), .b(negator_1_out), .out(Output), .cin(1'b0));  // open: cout
endmodule

module SUB4A (
  input  [3:0] Minuend,
  input  Borrow_In,
  input  [3:0] Subtrahend,
  output [3:0] Output,
  output Borrow_Out
);

  wire [3:0] adder_1_out;
  wire [4:0] negator_1_out;

  Adder #(.width(4)) adder_1 (.a({3'b000, Borrow_In}), .b(Subtrahend), .out(adder_1_out), .cin(1'b0));  // open: cout
  Negator #(.width(5)) negator_1 (.in({1'b0, adder_1_out}), .out(negator_1_out));
  Adder #(.width(5)) adder_2 (
    .a({1'b0, Minuend}), .b(negator_1_out), .out({Borrow_Out, Output}), .cin(1'b0));  // open: cout
endmodule

module SUB0 (
  input  Input_A,
  input  Input_B,
  input  Carry_In,
  output Output,
  output Carry_Out
);

  wire and_1_out, and_2_out, and_3_out, nor_1_out, nor_2_out, nor_3_out, not_1_out;

  nor nor_1 (nor_1_out, Input_B, Carry_In);
  nor nor_2 (nor_2_out, nor_1_out, and_1_out);
  and and_1 (and_1_out, Input_B, Carry_In);
  not not_1 (not_1_out, Input_A);
  nor nor_3 (nor_3_out, Input_A, nor_2_out);
  nor nor_4 (Output, nor_3_out, and_2_out);
  and and_2 (and_2_out, Input_A, nor_2_out);
  and and_3 (and_3_out, not_1_out, nor_2_out);
  or or_1 (Carry_Out, and_3_out, and_1_out);
endmodule

module SUB1 (
  input  Input_A,
  input  Input_B,
  input  Carry_In,
  output Output,
  output Carry_Out
);

  wire and_1_out, and_2_out, not_1_out, xor_1_out;

  not not_1 (not_1_out, Input_A);
  xor xor_1 (xor_1_out, Input_B, Carry_In);
  and and_1 (and_1_out, Input_B, Carry_In);
  xor xor_2 (Output, Input_A, xor_1_out);
  and and_2 (and_2_out, not_1_out, xor_1_out);
  or or_1 (Carry_Out, and_2_out, and_1_out);
endmodule

module SUBSP0 (
  input  Input_A,
  input  Input_B,
  output Output,
  output Carry_Out
);

  wire and_1_out, nor_1_out, not_1_out;

  not not_1 (not_1_out, Input_A);
  nor nor_1 (nor_1_out, Input_A, Input_B);
  nor nor_2 (Output, nor_1_out, and_1_out);
  and and_1 (and_1_out, Input_A, Input_B);
  and and_2 (Carry_Out, not_1_out, Input_B);
endmodule

module SUBSP1 (
  input  Input_A,
  input  Input_B,
  output Output,
  output Carry_Out
);

  wire not_1_out;

  not not_1 (not_1_out, Input_A);
  xor xor_1 (Output, Input_A, Input_B);
  and and_1 (Carry_Out, not_1_out, Input_B);
endmodule

module SUBSR0 (
  input  Input_A,
  input  Input_B,
  input  Carry_In,
  output Output
);

  wire and_1_out, and_2_out, nor_1_out, nor_2_out, nor_3_out;

  nor nor_1 (nor_1_out, Input_B, Carry_In);
  nor nor_2 (nor_2_out, nor_1_out, and_1_out);
  and and_1 (and_1_out, Input_B, Carry_In);
  nor nor_3 (nor_3_out, Input_A, nor_2_out);
  and and_2 (and_2_out, Input_A, nor_2_out);
  nor nor_4 (Output, nor_3_out, and_2_out);
endmodule

module SUBSR1 (
  input  Input_A,
  input  Input_B,
  input  Carry_In,
  output Output
);

  wire xor_2_out;

  xor xor_1 (Output, Input_A, xor_2_out);
  xor xor_2 (xor_2_out, Input_B, Carry_In);
endmodule

module SUB2B (
  input  Carry_In,
  input  [1:0] Input_A,
  input  [1:0] Input_B,
  output [1:0] Output,
  output Carry_Out
);

  wire sub0_1_carry_out;

  SUB0 sub0_1 (
    .Carry_In(Carry_In), .Input_A(Input_A[0]), .Input_B(Input_B[0]), .Output(Output[0]),
    .Carry_Out(sub0_1_carry_out));
  SUB0 sub0_2 (
    .Carry_In(sub0_1_carry_out), .Input_A(Input_A[1]), .Input_B(Input_B[1]), .Output(Output[1]),
    .Carry_Out(Carry_Out));
endmodule

module SUB4B (
  input  Carry_In,
  input  [3:0] Input_A,
  input  [3:0] Input_B,
  output [3:0] Output,
  output Carry_Out
);

  wire sub0_1_carry_out, sub0_2_carry_out, sub0_3_carry_out;

  SUB0 sub0_1 (
    .Carry_In(Carry_In), .Input_A(Input_A[0]), .Input_B(Input_B[0]), .Output(Output[0]),
    .Carry_Out(sub0_1_carry_out));
  SUB0 sub0_2 (
    .Carry_In(sub0_1_carry_out), .Input_A(Input_A[1]), .Input_B(Input_B[1]), .Output(Output[1]),
    .Carry_Out(sub0_2_carry_out));
  SUB0 sub0_3 (
    .Carry_In(sub0_2_carry_out), .Input_A(Input_A[2]), .Input_B(Input_B[2]), .Output(Output[2]),
    .Carry_Out(sub0_3_carry_out));
  SUB0 sub0_4 (
    .Carry_In(sub0_3_carry_out), .Input_A(Input_A[3]), .Input_B(Input_B[3]), .Output(Output[3]),
    .Carry_Out(Carry_Out));
endmodule

module SUB4B2 (
  input  Carry_In,
  input  [3:0] Input_A,
  input  [3:0] Input_B,
  output [3:0] Output,
  output Carry_Out
);

  wire sub2b_1_carry_out;

  SUB2B sub2b_1 (
    .Carry_In(Carry_In), .Input_A(Input_A[1:0]), .Input_B(Input_B[1:0]), .Output(Output[1:0]),
    .Carry_Out(sub2b_1_carry_out));
  SUB2B sub2b_2 (
    .Carry_In(sub2b_1_carry_out), .Input_A(Input_A[3:2]), .Input_B(Input_B[3:2]), .Output(Output[3:2]),
    .Carry_Out(Carry_Out));
endmodule

module list1 (
  output [7:0] out_1,
  output [7:0] out_2,
  output [7:0] out_3,
  output [7:0] out_4,
  output [7:0] out_5,
  output [7:0] out_6,
  output [7:0] out_7,
  output [7:0] out_8,
  output [7:0] out_9
);

  // Probe on 8'h5
  // Probe on 8'h7
  // Probe on 8'h14
  // Probe on 8'hf1
  // Probe on 8'h5
  // Probe on 8'h14
  // Probe on 8'h32
  // Probe on 8'h73
  // Probe on 8'h92

  assign out_1 = 8'h5;
  assign out_2 = 8'h7;
  assign out_3 = 8'h14;
  assign out_4 = 8'hf1;
  assign out_5 = 8'h5;
  assign out_6 = 8'h14;
  assign out_7 = 8'h32;
  assign out_8 = 8'h73;
  assign out_9 = 8'h92;
endmodule

module list2 (
  output [7:0] out_1,
  output [7:0] out_2,
  output [7:0] out_3,
  output [7:0] out_4,
  output [7:0] out_5,
  output [7:0] out_6,
  output [7:0] out_7,
  output [7:0] out_8,
  output [7:0] out_9
);

  // Probe on 8'h5
  // Probe on 8'h7
  // Probe on 8'h14
  // Probe on 8'ha
  // Probe on 8'hec
  // Probe on 8'hf1
  // Probe on 8'h32
  // Probe on 8'h73
  // Probe on 8'h92

  assign out_1 = 8'h5;
  assign out_2 = 8'h7;
  assign out_3 = 8'h14;
  assign out_4 = 8'ha;
  assign out_5 = 8'hec;
  assign out_6 = 8'hf1;
  assign out_7 = 8'h32;
  assign out_8 = 8'h73;
  assign out_9 = 8'h92;
endmodule

module main_ADD_OU_EX (
  input  Input_A,
  input  Input_A_2,
  input  A,
  input  Input_B,
  input  Input_B_2,
  input  B,
  input  Input_A_3,
  input  Input_A_4,
  input  Input_B_3,
  input  Input_B_4,
  input  Input_A_5,
  input  Input_B_5,
  input  Input_A_6,
  input  Input_B_6,
  output Output,
  output Output_2,
  output Carry_Out,
  output Carry_Out_2,
  output out_19,
  output Output_3,
  output Output_4,
  output out_22,
  output Carry_Out_3,
  output Carry_Out_4,
  output out_25,
  output Output_5,
  output Carry_Out_5,
  output out_28,
  output Output_6,
  output Carry_Out_6
);

  wire and_2_out, and_10_out, and_12_out, and_13_out, nand_1_out, nand_2_out, nor_1_out, nor_2_out,
       nor_5_out, not_1_out, not_2_out, not_3_out, or_1_out, or_2_out, or_3_out, or_4_out, or_5_out;

  or or_1 (or_1_out, Input_A, Input_B);
  and and_1 (Carry_Out, Input_A, Input_B);
  or or_2 (or_2_out, Input_A_3, Input_B_3);
  and and_2 (and_2_out, Input_A_3, Input_B_3);
  and and_3 (Carry_Out_3, Input_A_3, Input_B_3);
  or or_3 (or_3_out, Input_A_5, Input_B_5);
  nand nand_1 (nand_1_out, Input_A_5, Input_B_5);
  and and_4 (Carry_Out_5, Input_A_5, Input_B_5);
  and and_5 (Output, or_1_out, not_1_out);
  not not_1 (not_1_out, Carry_Out);
  and and_6 (Output_3, or_2_out, not_2_out);
  not not_2 (not_2_out, and_2_out);
  and and_7 (Output_5, or_3_out, nand_1_out);
  xor xor_1 (Output_6, Input_A_6, Input_B_6);
  and and_8 (Carry_Out_6, Input_A_6, Input_B_6);
  nor nor_1 (nor_1_out, Input_A_2, Input_B_2);
  and and_9 (Carry_Out_2, Input_A_2, Input_B_2);
  nor nor_2 (nor_2_out, Input_A_4, Input_B_4);
  and and_10 (and_10_out, Input_A_4, Input_B_4);
  and and_11 (Carry_Out_4, Input_A_4, Input_B_4);
  nor nor_3 (Output_2, nor_1_out, Carry_Out_2);
  nor nor_4 (Output_4, nor_2_out, and_10_out);
  nor nor_5 (nor_5_out, A, B);
  and and_12 (and_12_out, A, B);
  xor xor_2 (out_22, A, B);
  or or_4 (or_4_out, A, B);
  nand nand_2 (nand_2_out, A, B);
  or or_5 (or_5_out, A, B);
  and and_13 (and_13_out, A, B);
  not not_3 (not_3_out, and_13_out);
  nor nor_6 (out_19, nor_5_out, and_12_out);
  and and_14 (out_25, or_4_out, nand_2_out);
  and and_15 (out_28, or_5_out, not_3_out);
endmodule
